# Fritzing sketch clock (saved by Fritzing 0.9.2b)
breadboards: 1

parts:
  JACK1 = 2.1mm DC Barrel Jack
  D1 = Rectifier Diode [part_number=1N4001 package="300 mil [THT]"]
  R1 = Resistor [tolerance=±5% resistance=10k package="2512 [SMD]"]
  R2 = Resistor [tolerance=±5% resistance=2.2k package="0805 [SMD]"]
  R3 = Resistor [tolerance=±5% resistance=470 package="0603 [SMD]"]
  R4 = Resistor [tolerance=±5% resistance=4.7k package="1206 [SMD]"]
  Q1 = NPN-Transistor [package="TO92 [THT]"]
  Part1 = LightBlue Bean
  Part2 = ws2812b [package="smd 2812b"]
  R5 = PHOTOCELL [package=photocell]
  U1 = Voltage Regulator - 3.3V [package="TO220 [THT]"]
  C2 = Capacitor Polarized [package=cpol-radial-100uf-25v]
  C4 = Capacitor Polarized [package=cpol-radial-1000uf-25v]

nets:
  N1: JACK1.center, D1.anode
  GND: JACK1.switch, JACK1.sleeve, Part1.GND, Part2.VSS, R5.P$2, U1.GND, C2.-, C4.-
  N2: D1.cathode, R1.Pin_0, Part2.VDD, U1.input_voltage, C4.+
  N3: R1.Pin_1, R3.Pin_0, Q1.C
  N4: R2.Pin_0, Q1.B
  N5: R2.Pin_1, R4.Pin_0, Part1.BAT, U1.output_voltage, C2.+
  N6: R3.Pin_1, Part2.DIN
  N7: R4.Pin_1, Part1.AIN_A0, R5.P$1
  N8: Q1.E, Part1.D4/MISO

custom parts:
  2.1mm DC Barrel Jack: 2.1mm DC Barrel Jack with Thru-Hole Connectors (breadboardable)
